// Logisim project ThumbInstructor.circ as structural Verilog: 47 circuits, main circuit main
module main (
);

  wire button_1_out, clock_1_out, cpu_1_illegal, cpu_1_load, cpu_1_store, or_1_out;
  wire [2:0] cpu_1_memwidth;
  wire [15:0] rom_1_data;
  wire [31:0] cpu_1_memaddr, cpu_1_pc, cpu_1_storevalue, memory_1_loadvalue;

  Clock clock_1 (.out(clock_1_out));
  Button button_1 (.out(button_1_out));
  or or_1 (or_1_out, cpu_1_illegal, clock_1_out);
  CPU cpu_1 (
    .Instruction(rom_1_data), .LoadValue(memory_1_loadvalue), .Clock(or_1_out), .Reset(button_1_out),
    .Illegal(cpu_1_illegal), .MemWidth(cpu_1_memwidth), .Store(cpu_1_store), .Load(cpu_1_load),
    .MemAddr(cpu_1_memaddr), .StoreValue(cpu_1_storevalue), .PC(cpu_1_pc));
  ROM #(.addrWidth(24), .dataWidth(16)) rom_1 (.addr(cpu_1_pc[25:2]), .data(rom_1_data));
  Memory memory_1 (
    .Width(cpu_1_memwidth), .Store(cpu_1_store), .Load(cpu_1_load), .Address(cpu_1_memaddr),
    .StoreValue(cpu_1_storevalue), .Clock(or_1_out), .LoadValue(memory_1_loadvalue));

  // Notes on the sheet:
  //   contents of rom_1 (hex, n*v repeats v):
  //   93 50 113 80 81b3 20 2023 30 2203 0 ffff
endmodule

module Extractor (
  input  [31:0] Instruction,
  input  [2:0] Format,
  output [6:0] Opcode,
  output [4:0] RD,
  output [2:0] Funct3,
  output [4:0] RS1,
  output [4:0] RS2,
  output [6:0] funct7,
  output [31:0] Immediate
);

  Multiplexer #(.select(3), .width(32)) multiplexer_1 (
    .in1({{21{Instruction[31]}}, Instruction[30:20]}),
    .in2({{21{Instruction[31]}}, Instruction[30:25], Instruction[11:7]}),
    .in3({{20{Instruction[31]}}, Instruction[7], Instruction[30:25], Instruction[11:8], 1'b0}),
    .in4({Instruction[31:12], {12{1'b0}}}),
    .in5({{12{Instruction[31]}}, Instruction[19:12], Instruction[20], Instruction[30:21], 1'b0}),
    .in6({32{1'b0}}), .in7({32{1'b0}}), .out(Immediate), .sel(Format));  // open: in0

  assign Funct3 = Instruction[14:12];
  assign funct7 = Instruction[31:25];
  assign Opcode = Instruction[6:0];
  assign RD = Instruction[11:7];
  assign RS1 = Instruction[19:15];
  assign RS2 = Instruction[24:20];

  // Notes on the sheet:
  //   I-type
  //   S-type
  //   B-type
  //   U-type
  //   J-type
endmodule

module Registers16 (
  input  Write,
  input  [3:0] RD,
  input  Clock,
  input  [31:0] Data,
  input  [3:0] RS1,
  input  [3:0] RS2,
  output [31:0] Out1,
  output [31:0] Out2
);

  wire decoder_1_out0, decoder_1_out1, decoder_1_out2, decoder_1_out3, decoder_1_out4, decoder_1_out5,
       decoder_1_out6, decoder_1_out7, decoder_1_out8, decoder_1_out9, decoder_1_out10, decoder_1_out11,
       decoder_1_out12, decoder_1_out13, decoder_1_out14, decoder_1_out15;
  wire [31:0] register_1_q, register_2_q, register_3_q, register_4_q, register_5_q, register_6_q,
       register_7_q, register_8_q, register_9_q, register_10_q, register_11_q, register_12_q, register_13_q,
       register_14_q, register_15_q, register_16_q;

  Multiplexer #(.select(4), .width(32)) multiplexer_1 (
    .in0(register_1_q), .in1(register_2_q), .in2(register_3_q), .in3(register_4_q), .in4(register_5_q),
    .in5(register_6_q), .in6(register_7_q), .in7(register_8_q), .in8(register_9_q), .in9(register_10_q),
    .in10(register_11_q), .in11(register_12_q), .in12(register_13_q), .in13(register_14_q),
    .in14(register_15_q), .in15(register_16_q), .out(Out1), .sel(RS1));
  Multiplexer #(.select(4), .width(32)) multiplexer_2 (
    .in0(register_1_q), .in1(register_2_q), .in2(register_3_q), .in3(register_4_q), .in4(register_5_q),
    .in5(register_6_q), .in6(register_7_q), .in7(register_8_q), .in8(register_9_q), .in9(register_10_q),
    .in10(register_11_q), .in11(register_12_q), .in12(register_13_q), .in13(register_14_q),
    .in14(register_15_q), .in15(register_16_q), .out(Out2), .sel(RS2));
  Decoder #(.select(4)) decoder_1 (
    .out0(decoder_1_out0), .out1(decoder_1_out1), .out2(decoder_1_out2), .out3(decoder_1_out3),
    .out4(decoder_1_out4), .out5(decoder_1_out5), .out6(decoder_1_out6), .out7(decoder_1_out7),
    .out8(decoder_1_out8), .out9(decoder_1_out9), .out10(decoder_1_out10), .out11(decoder_1_out11),
    .out12(decoder_1_out12), .out13(decoder_1_out13), .out14(decoder_1_out14), .out15(decoder_1_out15),
    .sel(RD), .en(Write));
  Register #(.trigger("falling"), .width(32)) register_1 (
    .D(Data), .en(decoder_1_out0), .clk(Clock), .Q(register_1_q));  // open: clr
  Register #(.trigger("falling"), .width(32)) register_2 (
    .D(Data), .en(decoder_1_out1), .clk(Clock), .Q(register_2_q));  // open: clr
  Register #(.trigger("falling"), .width(32)) register_3 (
    .D(Data), .en(decoder_1_out2), .clk(Clock), .Q(register_3_q));  // open: clr
  Register #(.trigger("falling"), .width(32)) register_4 (
    .D(Data), .en(decoder_1_out3), .clk(Clock), .Q(register_4_q));  // open: clr
  Register #(.trigger("falling"), .width(32)) register_5 (
    .D(Data), .en(decoder_1_out4), .clk(Clock), .Q(register_5_q));  // open: clr
  Register #(.trigger("falling"), .width(32)) register_6 (
    .D(Data), .en(decoder_1_out5), .clk(Clock), .Q(register_6_q));  // open: clr
  Register #(.trigger("falling"), .width(32)) register_7 (
    .D(Data), .en(decoder_1_out6), .clk(Clock), .Q(register_7_q));  // open: clr
  Register #(.trigger("falling"), .width(32)) register_8 (
    .D(Data), .en(decoder_1_out7), .clk(Clock), .Q(register_8_q));  // open: clr
  Register #(.trigger("falling"), .width(32)) register_9 (
    .D(Data), .en(decoder_1_out8), .clk(Clock), .Q(register_9_q));  // open: clr
  Register #(.trigger("falling"), .width(32)) register_10 (
    .D(Data), .en(decoder_1_out9), .clk(Clock), .Q(register_10_q));  // open: clr
  Register #(.trigger("falling"), .width(32)) register_11 (
    .D(Data), .en(decoder_1_out10), .clk(Clock), .Q(register_11_q));  // open: clr
  Register #(.trigger("falling"), .width(32)) register_12 (
    .D(Data), .en(decoder_1_out11), .clk(Clock), .Q(register_12_q));  // open: clr
  Register #(.trigger("falling"), .width(32)) register_13 (
    .D(Data), .en(decoder_1_out12), .clk(Clock), .Q(register_13_q));  // open: clr
  Register #(.trigger("falling"), .width(32)) register_14 (
    .D(Data), .en(decoder_1_out13), .clk(Clock), .Q(register_14_q));  // open: clr
  Register #(.trigger("falling"), .width(32)) register_15 (
    .D(Data), .en(decoder_1_out14), .clk(Clock), .Q(register_15_q));  // open: clr
  Register #(.trigger("falling"), .width(32)) register_16 (
    .D(Data), .en(decoder_1_out15), .clk(Clock), .Q(register_16_q));  // open: clr
endmodule

module Registers16WithZero (
  input  Write,
  input  [3:0] RD,
  input  Clock,
  input  [31:0] Data,
  input  [3:0] RS1,
  input  [3:0] RS2,
  output [31:0] Out1,
  output [31:0] Out2
);

  wire decoder_1_out1, decoder_1_out2, decoder_1_out3, decoder_1_out4, decoder_1_out5, decoder_1_out6,
       decoder_1_out7, decoder_1_out8, decoder_1_out9, decoder_1_out10, decoder_1_out11, decoder_1_out12,
       decoder_1_out13, decoder_1_out14, decoder_1_out15;
  wire [31:0] register_1_q, register_2_q, register_3_q, register_4_q, register_5_q, register_6_q,
       register_7_q, register_8_q, register_9_q, register_10_q, register_11_q, register_12_q, register_13_q,
       register_14_q, register_15_q;

  Multiplexer #(.select(4), .width(32)) multiplexer_1 (
    .in0({32{1'b0}}), .in1(register_1_q), .in2(register_2_q), .in3(register_3_q), .in4(register_4_q),
    .in5(register_5_q), .in6(register_6_q), .in7(register_7_q), .in8(register_8_q), .in9(register_9_q),
    .in10(register_10_q), .in11(register_11_q), .in12(register_12_q), .in13(register_13_q),
    .in14(register_14_q), .in15(register_15_q), .out(Out1), .sel(RS1));
  Multiplexer #(.select(4), .width(32)) multiplexer_2 (
    .in0({32{1'b0}}), .in1(register_1_q), .in2(register_2_q), .in3(register_3_q), .in4(register_4_q),
    .in5(register_5_q), .in6(register_6_q), .in7(register_7_q), .in8(register_8_q), .in9(register_9_q),
    .in10(register_10_q), .in11(register_11_q), .in12(register_12_q), .in13(register_13_q),
    .in14(register_14_q), .in15(register_15_q), .out(Out2), .sel(RS2));
  Decoder #(.select(4)) decoder_1 (
    .out1(decoder_1_out1), .out2(decoder_1_out2), .out3(decoder_1_out3), .out4(decoder_1_out4),
    .out5(decoder_1_out5), .out6(decoder_1_out6), .out7(decoder_1_out7), .out8(decoder_1_out8),
    .out9(decoder_1_out9), .out10(decoder_1_out10), .out11(decoder_1_out11), .out12(decoder_1_out12),
    .out13(decoder_1_out13), .out14(decoder_1_out14), .out15(decoder_1_out15), .sel(RD), .en(Write));  // open: out0
  Register #(.trigger("falling"), .width(32)) register_1 (
    .D(Data), .en(decoder_1_out1), .clk(Clock), .Q(register_1_q));  // open: clr
  Register #(.trigger("falling"), .width(32)) register_2 (
    .D(Data), .en(decoder_1_out2), .clk(Clock), .Q(register_2_q));  // open: clr
  Register #(.trigger("falling"), .width(32)) register_3 (
    .D(Data), .en(decoder_1_out3), .clk(Clock), .Q(register_3_q));  // open: clr
  Register #(.trigger("falling"), .width(32)) register_4 (
    .D(Data), .en(decoder_1_out4), .clk(Clock), .Q(register_4_q));  // open: clr
  Register #(.trigger("falling"), .width(32)) register_5 (
    .D(Data), .en(decoder_1_out5), .clk(Clock), .Q(register_5_q));  // open: clr
  Register #(.trigger("falling"), .width(32)) register_6 (
    .D(Data), .en(decoder_1_out6), .clk(Clock), .Q(register_6_q));  // open: clr
  Register #(.trigger("falling"), .width(32)) register_7 (
    .D(Data), .en(decoder_1_out7), .clk(Clock), .Q(register_7_q));  // open: clr
  Register #(.trigger("falling"), .width(32)) register_8 (
    .D(Data), .en(decoder_1_out8), .clk(Clock), .Q(register_8_q));  // open: clr
  Register #(.trigger("falling"), .width(32)) register_9 (
    .D(Data), .en(decoder_1_out9), .clk(Clock), .Q(register_9_q));  // open: clr
  Register #(.trigger("falling"), .width(32)) register_10 (
    .D(Data), .en(decoder_1_out10), .clk(Clock), .Q(register_10_q));  // open: clr
  Register #(.trigger("falling"), .width(32)) register_11 (
    .D(Data), .en(decoder_1_out11), .clk(Clock), .Q(register_11_q));  // open: clr
  Register #(.trigger("falling"), .width(32)) register_12 (
    .D(Data), .en(decoder_1_out12), .clk(Clock), .Q(register_12_q));  // open: clr
  Register #(.trigger("falling"), .width(32)) register_13 (
    .D(Data), .en(decoder_1_out13), .clk(Clock), .Q(register_13_q));  // open: clr
  Register #(.trigger("falling"), .width(32)) register_14 (
    .D(Data), .en(decoder_1_out14), .clk(Clock), .Q(register_14_q));  // open: clr
  Register #(.trigger("falling"), .width(32)) register_15 (
    .D(Data), .en(decoder_1_out15), .clk(Clock), .Q(register_15_q));  // open: clr

  // Notes on the sheet:
  //   ZERO
  //   RA
  //   SP
  //   GP
  //   TP
  //   T0
  //   T1
  //   T2
  //   S0
  //   S1
  //   A0
  //   A1
  //   S2
  //   S3
  //   S4
  //   S5
endmodule

module RegisterFile (
  input  [31:0] Data,
  input  [4:0] RD,
  input  Write,
  input  Clock,
  input  [4:0] RS1,
  input  [4:0] RS2,
  output [31:0] Out1,
  output [31:0] Out2
);

  wire demultiplexer_1_out0, demultiplexer_1_out1;
  wire [31:0] BottomRegisters_out1, BottomRegisters_out2, TopRegisters_out1, TopRegisters_out2;

  Demultiplexer demultiplexer_1 (.out0(demultiplexer_1_out0), .out1(demultiplexer_1_out1), .in(Write), .sel(RD[4]));
  Registers16WithZero BottomRegisters (
    .Write(demultiplexer_1_out0), .RD(RD[3:0]), .Clock(Clock), .Data(Data), .RS1(RS1[3:0]), .RS2(RS2[3:0]),
    .Out1(BottomRegisters_out1), .Out2(BottomRegisters_out2));
  Registers16 TopRegisters (
    .Write(demultiplexer_1_out1), .RD(RD[3:0]), .Clock(Clock), .Data(Data), .RS1(RS1[3:0]), .RS2(RS2[3:0]),
    .Out1(TopRegisters_out1), .Out2(TopRegisters_out2));
  Multiplexer #(.width(32)) multiplexer_1 (
    .in0(BottomRegisters_out1), .in1(TopRegisters_out1), .out(Out1), .sel(RS1[4]));
  Multiplexer #(.width(32)) multiplexer_2 (
    .in0(BottomRegisters_out2), .in1(TopRegisters_out2), .out(Out2), .sel(RS2[4]));
endmodule

module CPU (
  input  [15:0] Instruction,
  input  [31:0] LoadValue,
  input  Clock,
  input  Reset,
  output Illegal,
  output [2:0] MemWidth,
  output Store,
  output Load,
  output [31:0] MemAddr,
  output [31:0] StoreValue,
  output [31:0] PC
);

  wire and_1_out, and_2_out, and_3_out, and_4_out, branchunit_1_branch, decoder_1_out0, decoder_1_out3,
       decoder_1_out4, decoder_1_out5, decoder_1_out8, decoder_1_out12, decoder_1_out13, decoder_1_out24,
       decoder_1_out25, decoder_1_out27, exmem_forward_pipe_1_write_out, fetchhalf_q,
       forwarding_unit_1_forwarda_exmem, forwarding_unit_1_forwarda_memwb, forwarding_unit_1_forwardb_exmem,
       forwarding_unit_1_forwardb_memwb, id_write_back_1_write_out, immediate_pipe_1_f_imm_to_alu_out,
       immediate_pipe_1_f_imm_to_data_out, immediate_pipe_1_f_imm_to_puls_pc_out,
       jalr_result_1_jalr_flag_out, load_flag_pipe_1_load_data, multiplexer_1_out, nand_1_out, nor_1_out,
       not_1_out, not_2_out, not_3_out, not_4_out, or_1_out, or_2_out, or_3_out, or_5_out, or_6_out,
       or_7_out, or_8_out, priority_encoder_1_p3, priority_encoder_1_p8, register_2_q,
       relative_jump_flags_pipe_1_relativejumpflag_out, signals_off_nooperation_1_s2_out,
       signals_off_nooperation_1_s3_out, signals_off_nooperation_1_s4_out, signals_off_nooperation_1_s5_out,
       signals_off_nooperation_1_s6_out, signals_off_nooperation_1_s7_out, signals_off_nooperation_1_s8_out,
       signals_off_nooperation_1_s9_out, signals_off_nooperation_1_s10_out, ThumbToggle_q,
       write_back_data_1_write_flag_out, write_back_pc_1_signal_out, xor_1_out, xor_2_out;
  wire [1:0] extractor_1_opcode;
  wire [2:0] extractor_1_funct3, id_exc1_1_funct3_out, priority_encoder_1_p6;
  wire [4:0] exmem_forward_pipe_1_rd_out, extractor_1_opcode_2, extractor_1_rd, extractor_1_rs1,
       extractor_1_rs2, id_exc1_1_rs1_out, id_exc1_1_rs2_out, id_write_back_1_rd_out;
  wire [6:0] extractor_1_funct7, id_exc1_1_funct7_out;
  wire [15:0] register_1_q;
  wire [31:0] a_to_memaddr_1_a_out, adder_1_out, adder_2_out, adder_3_out, adder_4_out, alu_1_data,
       controlled_buffer_1_out, controlled_buffer_4_out, exmem_forward_pipe_1_aluresult_out,
       extractor_1_immediate, id_exc1_1_out1_out, id_exc1_1_out2_out, immediate_pipe_1_to_alu,
       immediate_pipe_1_to_memwidth, immediate_pipe_1_to_write_back, instructions_32bits_1_instructions_out,
       jalr_result_1_sum_out, multiplexer_2_out, multiplexer_3_out, multiplexer_4_out, multiplexer_5_out,
       multiplexer_6_out, multiplexer_7_out, register_4_q, register_6_q, register_7_q, register_8_q,
       register_9_q, register_10_q, registerfile_1_out1, registerfile_1_out2, store_pc_1_pc_out,
       subtractor_1_out, thumb_decompresser_1_instruction_out, write_back_data_1_data_out;

  xor xor_1 (xor_1_out, fetchhalf_q, 1'b1);
  Register #(.trigger("falling"), .width(1)) fetchhalf (
    .D(multiplexer_1_out), .clk(Clock), .Q(fetchhalf_q));  // open: en, clr
  Multiplexer multiplexer_1 (.in0(xor_1_out), .in1(1'b0), .out(multiplexer_1_out), .sel(ThumbToggle_q));
  not not_1 (not_1_out, fetchhalf_q);
  Register #(.trigger("falling"), .width(16)) register_1 (
    .D(Instruction), .en(not_1_out), .clk(Clock), .Q(register_1_q));  // open: clr
  Register #(.trigger("falling"), .width(1)) register_2 (
    .D(and_1_out), .clk(Clock), .Q(register_2_q));  // open: en, clr
  and and_1 (and_1_out, extractor_1_opcode[0], extractor_1_opcode[1], extractor_1_opcode_2[0], extractor_1_opcode_2[1], extractor_1_opcode_2[2], extractor_1_opcode_2[3], extractor_1_opcode_2[4]);
  or or_1 (or_1_out, ThumbToggle_q, fetchhalf_q);
  not not_2 (not_2_out, register_2_q);
  Instructions_32Bits instructions_32bits_1 (
    .LowerHalf(register_1_q), .UpperHalf(Instruction),
    .Instructions_OUT(instructions_32bits_1_instructions_out));
  Thumb_Decompresser thumb_decompresser_1 (
    .Instruction_IN(Instruction), .Instruction_OUT(thumb_decompresser_1_instruction_out));
  and and_2 (and_2_out, and_1_out, not_2_out);
  Multiplexer #(.width(32)) multiplexer_2 (
    .in0(instructions_32bits_1_instructions_out), .in1(thumb_decompresser_1_instruction_out),
    .out(multiplexer_2_out), .sel(ThumbToggle_q));
  Register #(.width(32)) register_3 (.D(thumb_decompresser_1_instruction_out), .clk(Clock));  // open: en, Q, clr
  and and_3 (and_3_out, Clock, or_1_out);
  Register #(.trigger("falling"), .width(1)) ThumbToggle (
    .D(xor_2_out), .clk(Clock), .Q(ThumbToggle_q), .clr(1'b0));  // open: en
  xor xor_2 (xor_2_out, ThumbToggle_q, and_2_out);
  Register #(.trigger("falling"), .width(32)) register_4 (
    .D(multiplexer_2_out), .clk(and_3_out), .Q(register_4_q), .clr(not_3_out));  // open: en
  not not_3 (not_3_out, nor_1_out);
  Extractor extractor_1 (
    .Instruction(register_4_q), .Format(priority_encoder_1_p6),
    .Opcode({extractor_1_opcode_2, extractor_1_opcode}), .RD(extractor_1_rd), .Funct3(extractor_1_funct3),
    .RS1(extractor_1_rs1), .RS2(extractor_1_rs2), .funct7(extractor_1_funct7),
    .Immediate(extractor_1_immediate));
  Register #(.trigger("falling"), .width(32)) register_5 (
    .D(subtractor_1_out), .clk(Clock), .Q(PC), .clr(Reset));  // open: en
  ID_Write_Back id_write_back_1 (
    .RD_IN(extractor_1_rd), .Write_IN(signals_off_nooperation_1_s9_out), .Clock(and_3_out),
    .RD_OUT(id_write_back_1_rd_out), .Write_OUT(id_write_back_1_write_out));
  Register #(.trigger("falling"), .width(32)) register_6 (.D(PC), .clk(Clock), .Q(register_6_q));  // open: en, clr
  EXMEM_Forward_Pipe exmem_forward_pipe_1 (
    .ALUResult_IN(alu_1_data), .RD_IN(extractor_1_rd), .Write_IN(signals_off_nooperation_1_s9_out),
    .Clock(and_3_out), .ALUResult_OUT(exmem_forward_pipe_1_aluresult_out),
    .RD_OUT(exmem_forward_pipe_1_rd_out), .Write_OUT(exmem_forward_pipe_1_write_out));
  Register #(.trigger("falling"), .width(32)) register_7 (
    .D(register_6_q), .clk(Clock), .Q(register_7_q));  // open: en, clr
  Register #(.trigger("falling"), .width(32)) register_8 (
    .D(register_7_q), .clk(Clock), .Q(register_8_q));  // open: en, clr
  assign controlled_buffer_1_out = jalr_result_1_jalr_flag_out ? jalr_result_1_sum_out : 32'bz;  // Controlled_Buffer controlled_buffer_1
  Subtractor #(.width(32)) subtractor_1 (
    .a(controlled_buffer_1_out), .b(32'h4), .out(subtractor_1_out));  // open: bin, bout
  assign controlled_buffer_1_out = relative_jump_flags_pipe_1_relativejumpflag_out ? adder_1_out : 32'bz;  // Controlled_Buffer controlled_buffer_2
  Adder #(.width(32)) adder_1 (.a(register_6_q), .b(immediate_pipe_1_to_alu), .out(adder_1_out));  // open: cin, cout
  nor nor_1 (nor_1_out, jalr_result_1_jalr_flag_out, relative_jump_flags_pipe_1_relativejumpflag_out);
  assign subtractor_1_out = nor_1_out ? adder_2_out : 32'bz;  // Controlled_Buffer controlled_buffer_3
  RegisterFile registerfile_1 (
    .Data(controlled_buffer_4_out), .RD(id_write_back_1_rd_out), .Write(id_write_back_1_write_out),
    .Clock(and_3_out), .RS1(extractor_1_rs1), .RS2(extractor_1_rs2), .Out1(registerfile_1_out1),
    .Out2(registerfile_1_out2));
  Immediate_PIPE immediate_pipe_1 (
    .Immediate_IN(extractor_1_immediate), .F_IMM_TO_DATA_IN(signals_off_nooperation_1_s7_out),
    .F_IMM_TO_PULS_PC_IN(signals_off_nooperation_1_s3_out),
    .F_IMM_TO_ALU_IN(signals_off_nooperation_1_s10_out), .Clock(and_3_out), .To_ALU(immediate_pipe_1_to_alu),
    .To_MemWidth(immediate_pipe_1_to_memwidth), .To_Write_Back(immediate_pipe_1_to_write_back),
    .F_IMM_TO_DATA_OUT(immediate_pipe_1_f_imm_to_data_out),
    .F_IMM_TO_PULS_PC_OUT(immediate_pipe_1_f_imm_to_puls_pc_out),
    .F_IMM_TO_ALU_OUT(immediate_pipe_1_f_imm_to_alu_out));
  Register #(.trigger("falling"), .width(32)) register_9 (
    .D(register_8_q), .clk(Clock), .Q(register_9_q));  // open: en, clr
  Adder #(.width(32)) adder_2 (.a(PC), .b(32'h4), .out(adder_2_out));  // open: cin, cout
  assign controlled_buffer_4_out = immediate_pipe_1_f_imm_to_data_out ? immediate_pipe_1_to_write_back : 32'bz;  // Controlled_Buffer controlled_buffer_4
  assign controlled_buffer_4_out = immediate_pipe_1_f_imm_to_puls_pc_out ? adder_3_out : 32'bz;  // Controlled_Buffer controlled_buffer_5
  Adder #(.width(32)) adder_3 (
    .a(immediate_pipe_1_to_write_back), .b(register_9_q), .out(adder_3_out));  // open: cin, cout
  ID_EXC1 id_exc1_1 (
    .RS1_IN(extractor_1_rs1), .RS2_IN(extractor_1_rs2), .FUNCT3_IN(extractor_1_funct3),
    .FUNCT7_IN(extractor_1_funct7), .OUT1_IN(registerfile_1_out1), .OUT2_IN(registerfile_1_out2),
    .CLOCK(and_3_out), .RS1_OUT(id_exc1_1_rs1_out), .RS2_OUT(id_exc1_1_rs2_out),
    .FUNCT3_OUT(id_exc1_1_funct3_out), .FUNCT7_OUT(id_exc1_1_funct7_out), .OUT1_OUT(id_exc1_1_out1_out),
    .OUT2_OUT(id_exc1_1_out2_out));
  Decoder #(.select(5)) decoder_1 (
    .out0(decoder_1_out0), .out3(decoder_1_out3), .out4(decoder_1_out4), .out5(decoder_1_out5),
    .out8(decoder_1_out8), .out12(decoder_1_out12), .out13(decoder_1_out13), .out24(decoder_1_out24),
    .out25(decoder_1_out25), .out27(decoder_1_out27), .sel(extractor_1_opcode_2));  // open: out1, out2, out6, out7, out9, out10, out11, out14, out15, out16, out17, out18, out19, out20, out21, out22, out23, out26, out28, out29, out30, out31, en
  nand nand_1 (nand_1_out, extractor_1_opcode[1], extractor_1_opcode[0]);
  Multiplexer #(.width(32)) multiplexer_3 (
    .in0(id_exc1_1_out1_out), .in1(controlled_buffer_4_out), .out(multiplexer_3_out),
    .sel(forwarding_unit_1_forwarda_memwb));
  assign controlled_buffer_4_out = write_back_pc_1_signal_out ? store_pc_1_pc_out : 32'bz;  // Controlled_Buffer controlled_buffer_6
  Store_pc store_pc_1 (.pc_in(adder_2_out), .Clock(and_3_out), .pc_out(store_pc_1_pc_out));
  or or_2 (or_2_out, nand_1_out, not_4_out);
  Multiplexer #(.width(32)) multiplexer_4 (
    .in0(id_exc1_1_out2_out), .in1(controlled_buffer_4_out), .out(multiplexer_4_out),
    .sel(forwarding_unit_1_forwardb_memwb));
  Multiplexer #(.width(32)) multiplexer_5 (
    .in0(multiplexer_4_out), .in1(exmem_forward_pipe_1_aluresult_out), .out(multiplexer_5_out),
    .sel(forwarding_unit_1_forwardb_exmem));
  not not_4 (not_4_out, priority_encoder_1_p8);
  Multiplexer #(.width(32)) multiplexer_6 (
    .in0(multiplexer_3_out), .in1(exmem_forward_pipe_1_aluresult_out), .out(multiplexer_6_out),
    .sel(forwarding_unit_1_forwarda_exmem));
  or or_3 (or_3_out, decoder_1_out13, decoder_1_out5);
  // Priority_Encoder priority_encoder_1: pin names not known; wires that end beside it: or_2_out, decoder_1_out12, priority_encoder_1_p3, decoder_1_out8, decoder_1_out24, priority_encoder_1_p6, or_3_out, priority_encoder_1_p8, decoder_1_out27, 1'b0, 1'b0
  Multiplexer #(.width(32)) multiplexer_7 (
    .in0(multiplexer_5_out), .in1(immediate_pipe_1_to_alu), .out(multiplexer_7_out),
    .sel(immediate_pipe_1_f_imm_to_alu_out));
  JALR_Result jalr_result_1 (
    .SUM_IN(adder_4_out), .JALR_FLAG_IN(signals_off_nooperation_1_s4_out), .CLOCK(and_3_out),
    .SUM_OUT(jalr_result_1_sum_out), .JALR_FLAG_OUT(jalr_result_1_jalr_flag_out));
  Write_back_PC write_back_pc_1 (.signal_IN(or_5_out), .CLOCK(and_3_out), .signal_OUT(write_back_pc_1_signal_out));
  Forwarding_Unit forwarding_unit_1 (
    .RS1(id_exc1_1_rs1_out), .EXMEM_RD(exmem_forward_pipe_1_rd_out),
    .EXMEM_Write(exmem_forward_pipe_1_write_out), .MEMWB_RD(id_write_back_1_rd_out),
    .MEMWB_Write(id_write_back_1_write_out), .RS2(id_exc1_1_rs2_out),
    .ForwardA_EXMEM(forwarding_unit_1_forwarda_exmem), .ForwardA_MEMWB(forwarding_unit_1_forwarda_memwb),
    .ForwardB_EXMEM(forwarding_unit_1_forwardb_exmem), .ForwardB_MEMWB(forwarding_unit_1_forwardb_memwb));
  or or_4 (priority_encoder_1_p3, decoder_1_out3, decoder_1_out4, decoder_1_out0, decoder_1_out25);
  or or_5 (or_5_out, signals_off_nooperation_1_s4_out, signals_off_nooperation_1_s5_out);
  or or_6 (or_6_out, decoder_1_out25, decoder_1_out12, decoder_1_out4, decoder_1_out0, decoder_1_out5, decoder_1_out13, decoder_1_out27);
  Adder #(.width(32)) adder_4 (
    .a(registerfile_1_out1), .b(extractor_1_immediate), .out(adder_4_out));  // open: cin, cout
  Relative_Jump_flags_PIPE relative_jump_flags_pipe_1 (
    .RelativeJumpFlag_IN(or_7_out), .CLOCK(and_3_out),
    .RelativeJumpFlag_OUT(relative_jump_flags_pipe_1_relativejumpflag_out));
  or or_7 (or_7_out, and_4_out, signals_off_nooperation_1_s5_out);
  or or_8 (or_8_out, decoder_1_out12, decoder_1_out4);
  and and_4 (and_4_out, branchunit_1_branch, signals_off_nooperation_1_s6_out);
  ALU alu_1 (
    .A(multiplexer_6_out), .B(multiplexer_7_out), .Funct3(id_exc1_1_funct3_out),
    .funct7(id_exc1_1_funct7_out), .Imm(immediate_pipe_1_f_imm_to_alu_out), .Data(alu_1_data));
  assign controlled_buffer_4_out = write_back_data_1_write_flag_out ? write_back_data_1_data_out : 32'bz;  // Controlled_Buffer controlled_buffer_7
  BranchUnit branchunit_1 (
    .A(registerfile_1_out1), .B(registerfile_1_out2), .Funct3(extractor_1_funct3),
    .Branch(branchunit_1_branch));
  Write_back_Data write_back_data_1 (
    .Write_Flag_IN(signals_off_nooperation_1_s8_out), .Data_IN(alu_1_data), .CLOCK(and_3_out),
    .Write_Flag_OUT(write_back_data_1_write_flag_out), .Data_OUT(write_back_data_1_data_out));
  Signals_off_NoOperation signals_off_nooperation_1 (
    .S1(decoder_1_out8), .S2(decoder_1_out0), .S3(decoder_1_out5), .S4(decoder_1_out25),
    .S5(decoder_1_out27), .S6(decoder_1_out24), .S7(decoder_1_out13), .S8(or_8_out), .S9(or_6_out),
    .S10(decoder_1_out4), .S_OFF(not_3_out), .S1_OUT(Store), .S2_OUT(signals_off_nooperation_1_s2_out),
    .S3_OUT(signals_off_nooperation_1_s3_out), .S4_OUT(signals_off_nooperation_1_s4_out),
    .S5_OUT(signals_off_nooperation_1_s5_out), .S6_OUT(signals_off_nooperation_1_s6_out),
    .S7_OUT(signals_off_nooperation_1_s7_out), .S8_OUT(signals_off_nooperation_1_s8_out),
    .S9_OUT(signals_off_nooperation_1_s9_out), .S10_OUT(signals_off_nooperation_1_s10_out));
  FUNCT3_TO_MemWidth funct3_to_memwidth_1 (.FUNCT3_IN(id_exc1_1_funct3_out), .CLOCK(and_3_out), .FUNCT3_OUT(MemWidth));
  Load_flag_PIPE load_flag_pipe_1 (
    .Load_flag_IN(signals_off_nooperation_1_s2_out), .CLOCK(and_3_out),
    .Load_data(load_flag_pipe_1_load_data), .Load_Mem(Load));
  A_TO_MemAddr a_to_memaddr_1 (.A_IN(multiplexer_6_out), .CLOCK(and_3_out), .A_OUT(a_to_memaddr_1_a_out));
  B_TO_StoreValue b_to_storevalue_1 (.B_IN(multiplexer_7_out), .CLOCK(and_3_out), .B_OUT(StoreValue));
  assign controlled_buffer_4_out = load_flag_pipe_1_load_data ? register_10_q : 32'bz;  // Controlled_Buffer controlled_buffer_8
  Adder #(.width(32)) adder_5 (
    .a(a_to_memaddr_1_a_out), .b(immediate_pipe_1_to_memwidth), .out(MemAddr));  // open: cin, cout
  Register #(.trigger("falling"), .width(32)) register_10 (
    .D(LoadValue), .clk(and_3_out), .Q(register_10_q));  // open: en, clr

  assign Illegal = 1'b0;

  // Notes on the sheet:
  //   AUIPC
  //   Store PC?
  //   Relative Jump?
  //   JALR
endmodule

module ALU (
  input  [31:0] A,
  input  [31:0] B,
  input  [2:0] Funct3,
  input  [6:0] funct7,
  input  Imm,
  output [31:0] Data
);

  wire and_2_out, and_3_out, not_1_out;
  wire [0:0] comparator_1_lt, comparator_2_lt;
  wire [31:0] adder_1_out, and_1_out, divider_1_out, divider_1_rem, divider_2_out, divider_2_rem,
       multiplexer_1_out, multiplexer_2_out, multiplexer_3_out, multiplexer_4_out, multiplexer_6_out,
       negator_1_out, or_1_out, shifter_1_out, shifter_2_out, shifter_3_out, subtractor_1_out, xor_1_out;
  wire [63:0] multiplier_1_out, multiplier_2_out, multiplier_3_out, negator_2_out;

  not not_1 (not_1_out, Imm);
  assign xor_1_out = A ^ B;  // XOR_Gate xor_1, 32 bits wide
  assign or_1_out = A | B;  // OR_Gate or_1, 32 bits wide
  assign and_1_out = A & B;  // AND_Gate and_1, 32 bits wide
  Shifter #(.width(32)) shifter_1 (.in(A), .\dist (B[4:0]), .out(shifter_1_out));
  Shifter #(.shift("lr"), .width(32)) shifter_2 (.in(A), .\dist (B[4:0]), .out(shifter_2_out));
  Shifter #(.shift("ar"), .width(32)) shifter_3 (.in(A), .\dist (B[4:0]), .out(shifter_3_out));
  Negator #(.width(32)) negator_1 (.in(B), .out(negator_1_out));
  Adder #(.width(32)) adder_1 (.a(A), .b(B), .out(adder_1_out));  // open: cin, cout
  Subtractor #(.width(32)) subtractor_1 (.a(A), .b(B), .out(subtractor_1_out));  // open: bin, bout
  and and_2 (and_2_out, funct7[5], not_1_out);
  Comparator #(.width(32)) comparator_1 (.a(A), .b(B), .lt(comparator_1_lt[0]));  // open: gt, eq
  Comparator #(.mode("unsigned"), .width(32)) comparator_2 (.a(A), .b(B), .lt(comparator_2_lt[0]));  // open: gt, eq
  Multiplexer #(.width(32)) multiplexer_1 (
    .in0(shifter_2_out), .in1(shifter_3_out), .out(multiplexer_1_out), .sel(funct7[5]));
  Multiplexer #(.width(32)) multiplexer_2 (
    .in0(adder_1_out), .in1(subtractor_1_out), .out(multiplexer_2_out), .sel(and_2_out));
  Divider #(.width(32)) divider_1 (.a(A), .b(B), .out(divider_1_out), .rem(divider_1_rem));  // open: upper
  Divider #(.mode("twosComplement"), .width(32)) divider_2 (
    .a(A), .b(B), .out(divider_2_out), .rem(divider_2_rem));  // open: upper
  Multiplexer #(.select(3), .width(32)) multiplexer_3 (
    .in0(multiplier_3_out[31:0]), .in1(multiplier_3_out[63:32]), .in2(multiplexer_6_out),
    .in3(multiplier_2_out[63:32]), .in4(divider_2_out), .in5(divider_1_out), .in6(divider_2_rem),
    .in7(divider_1_rem), .out(multiplexer_3_out), .sel(Funct3));
  Multiplexer #(.select(3), .width(32)) multiplexer_4 (
    .in0(multiplexer_2_out), .in1(shifter_1_out), .in2({{31{1'b0}}, comparator_1_lt[0]}),
    .in3({{31{1'b0}}, comparator_2_lt[0]}), .in4(xor_1_out), .in5(multiplexer_1_out), .in6(or_1_out),
    .in7(and_1_out), .out(multiplexer_4_out), .sel(Funct3));
  Multiplier #(.width(64)) multiplier_1 (
    .a({{32{1'b0}}, negator_1_out}), .b({{32{1'b0}}, A}), .out(multiplier_1_out));  // open: cin, cout
  Multiplexer #(.width(32)) multiplexer_5 (
    .in0(multiplexer_4_out), .in1(multiplexer_3_out), .out(Data), .sel(and_3_out));
  and and_3 (and_3_out, funct7[0], ~Imm);  // AND_Gate
  Negator #(.width(64)) negator_2 (.in(multiplier_1_out), .out(negator_2_out));
  Multiplier #(.width(64)) multiplier_2 (
    .a({{32{1'b0}}, B}), .b({{32{1'b0}}, A}), .out(multiplier_2_out));  // open: cin, cout
  Multiplexer #(.width(32)) multiplexer_6 (
    .in0(negator_2_out[63:32]), .in1(multiplier_2_out[63:32]), .out(multiplexer_6_out),
    .sel(negator_1_out[31]));
  Multiplier #(.mode("twosComplement"), .width(64)) multiplier_3 (
    .a({{33{B[31]}}, B[30:0]}), .b({{33{A[31]}}, A[30:0]}), .out(multiplier_3_out));  // open: cin, cout
endmodule

module BranchUnit (
  input  [31:0] A,
  input  [31:0] B,
  input  [2:0] Funct3,
  output Branch
);

  wire comparator_1_eq, comparator_1_gt, comparator_1_lt, comparator_2_eq, comparator_2_gt, comparator_2_lt,
       not_1_out, or_1_out, or_2_out;

  Comparator #(.mode("unsigned"), .width(32)) comparator_1 (
    .a(A), .b(B), .gt(comparator_1_gt), .eq(comparator_1_eq), .lt(comparator_1_lt));
  Comparator #(.width(32)) comparator_2 (
    .a(A), .b(B), .gt(comparator_2_gt), .eq(comparator_2_eq), .lt(comparator_2_lt));
  not not_1 (not_1_out, comparator_1_eq);
  or or_1 (or_1_out, comparator_1_gt, comparator_1_eq);
  or or_2 (or_2_out, comparator_2_gt, comparator_2_eq);
  Multiplexer #(.select(3)) multiplexer_1 (
    .in0(comparator_1_eq), .in1(not_1_out), .in2(1'b0), .in3(1'b0), .in4(comparator_2_lt), .in5(or_2_out),
    .in6(comparator_1_lt), .in7(or_1_out), .out(Branch), .sel(Funct3));
endmodule

module Memory (
  input  [2:0] Width,
  input  Store,
  input  Load,
  input  [31:0] Address,
  input  [31:0] StoreValue,
  input  Clock,
  output [31:0] LoadValue
);

  wire not_1_out, not_2_out, not_3_out, not_4_out, or_1_out;
  wire [1:0] subtractor_1_out_2;
  wire [31:0] multiplexer_1_out, multiplexer_2_out, multiplexer_3_out, multiplexer_4_out, multiplexer_5_out,
       multiplexer_7_out, multiplexer_8_out, multiplexer_9_out, multiplexer_10_out, multiplexer_11_out,
       multiplexer_12_out, ram_1_dout, ram_1_dout_2;
  wire [31:2] subtractor_1_out;
  wire [31:8] ram_1_dout_3, ram_1_dout_4;

  Subtractor #(.width(32)) subtractor_1 (
    .a(Address), .b(32'h1000000), .out({subtractor_1_out, subtractor_1_out_2}));  // open: bin, bout
  or or_1 (or_1_out, Store, Load);
  Multiplexer #(.width(32)) multiplexer_1 (
    .in0({ram_1_dout_4[31], ram_1_dout_4[14:8], ram_1_dout_3[31], ram_1_dout_3[14:8], StoreValue[15:0]}),
    .in1({ram_1_dout_4[31], ram_1_dout_4[14:8], StoreValue[15:0], ram_1_dout[31], ram_1_dout[6:0]}),
    .out(multiplexer_1_out), .sel(subtractor_1_out_2[0]));
  Multiplexer #(.width(32)) multiplexer_2 (
    .in0(multiplexer_1_out),
    .in1({StoreValue[15:0], ram_1_dout_2[31], ram_1_dout_2[6:0], ram_1_dout[31], ram_1_dout[6:0]}),
    .out(multiplexer_2_out), .sel(subtractor_1_out_2[1]));
  Multiplexer #(.select(2), .width(32)) multiplexer_3 (
    .in0({ram_1_dout_4[31], ram_1_dout_4[14:8], ram_1_dout_3[31], ram_1_dout_3[14:8], ram_1_dout_2[31], ram_1_dout_2[6:0], StoreValue[7:0]}),
    .in1({ram_1_dout_4[31], ram_1_dout_4[14:8], ram_1_dout_3[31], ram_1_dout_3[14:8], StoreValue[7:0], ram_1_dout[31], ram_1_dout[6:0]}),
    .in2({ram_1_dout_4[31], ram_1_dout_4[14:8], StoreValue[7:0], ram_1_dout_2[31], ram_1_dout_2[6:0], ram_1_dout[31], ram_1_dout[6:0]}),
    .in3({StoreValue[7:0], ram_1_dout_3[31], ram_1_dout_3[14:8], ram_1_dout_2[31], ram_1_dout_2[6:0], ram_1_dout[31], ram_1_dout[6:0]}),
    .out(multiplexer_3_out), .sel(subtractor_1_out_2));
  Multiplexer #(.width(32)) multiplexer_4 (
    .in0(StoreValue), .in1(multiplexer_5_out), .out(multiplexer_4_out), .sel(not_1_out));
  not not_1 (not_1_out, Width[1]);
  not not_2 (not_2_out, Width[0]);
  Multiplexer #(.width(32)) multiplexer_5 (
    .in0(multiplexer_2_out), .in1(multiplexer_3_out), .out(multiplexer_5_out), .sel(not_2_out));
  RAM #(.addrWidth(24), .asyncread("true"), .dataWidth(32), .trigger("falling")) ram_1 (
    .addr(subtractor_1_out[25:2]), .we(Store), .oe(or_1_out), .clk(Clock), .din(multiplexer_4_out),
    .dout({ram_1_dout_4[31], ram_1_dout_4[14:8], ram_1_dout_3[31], ram_1_dout_3[14:8], ram_1_dout_2[31], ram_1_dout_2[6:0], ram_1_dout[31], ram_1_dout[6:0]}));
  Multiplexer #(.width(32)) multiplexer_6 (
    .in0({ram_1_dout_4[31], ram_1_dout_4[14:8], ram_1_dout_3[31], ram_1_dout_3[14:8], ram_1_dout_2[31], ram_1_dout_2[6:0], ram_1_dout[31], ram_1_dout[6:0]}),
    .in1(multiplexer_8_out), .out(LoadValue), .sel(not_3_out));
  not not_3 (not_3_out, Width[1]);
  not not_4 (not_4_out, Width[0]);
  Multiplexer #(.width(32)) multiplexer_7 (
    .in0({{17{ram_1_dout_2[31]}}, ram_1_dout_2[6:0], ram_1_dout[31], ram_1_dout[6:0]}),
    .in1({{17{ram_1_dout_3[31]}}, ram_1_dout_3[14:8], ram_1_dout_2[31], ram_1_dout_2[6:0]}),
    .out(multiplexer_7_out), .sel(subtractor_1_out_2[0]));
  Multiplexer #(.width(32)) multiplexer_8 (
    .in0(multiplexer_11_out), .in1(multiplexer_12_out), .out(multiplexer_8_out), .sel(not_4_out));
  Multiplexer #(.width(32)) multiplexer_9 (
    .in0(multiplexer_7_out),
    .in1({{17{ram_1_dout_4[31]}}, ram_1_dout_4[14:8], ram_1_dout_3[31], ram_1_dout_3[14:8]}),
    .out(multiplexer_9_out), .sel(subtractor_1_out_2[1]));
  Multiplexer #(.select(2), .width(32)) multiplexer_10 (
    .in0({{25{ram_1_dout[31]}}, ram_1_dout[6:0]}), .in1({{25{ram_1_dout_2[31]}}, ram_1_dout_2[6:0]}),
    .in2({{25{ram_1_dout_3[31]}}, ram_1_dout_3[14:8]}), .in3({{25{ram_1_dout_4[31]}}, ram_1_dout_4[14:8]}),
    .out(multiplexer_10_out), .sel(subtractor_1_out_2));
  Multiplexer #(.width(32)) multiplexer_11 (
    .in0(multiplexer_9_out), .in1({{16{1'b0}}, multiplexer_9_out[15:0]}), .out(multiplexer_11_out),
    .sel(Width[2]));
  Multiplexer #(.width(32)) multiplexer_12 (
    .in0(multiplexer_10_out), .in1({{24{1'b0}}, multiplexer_10_out[7:0]}), .out(multiplexer_12_out),
    .sel(Width[2]));
endmodule

module IF_REG (
);

  wire undriven_2, undriven_3;
  wire [31:0] undriven;

  Register #(.width(32)) register_1 (.D(undriven), .en(undriven_2), .clk(undriven_3));  // open: Q, clr
endmodule

module ID_REGFILE_PIPE (
  input  [4:0] RS1_IN,
  input  [4:0] RS2_IN,
  input  CLOCK,
  output [4:0] RS1_OUT,
  output [4:0] RS2_OUT
);

  Register #(.width(5)) RS1 (.D(RS1_IN), .clk(CLOCK), .Q(RS1_OUT));  // open: en, clr
  Register #(.width(5)) RS2 (.D(RS2_IN), .clk(CLOCK), .Q(RS2_OUT));  // open: en, clr
endmodule

module ID_EXC_PIPE (
  input  [2:0] FUNCT3_IN,
  input  [6:0] FUNCT7_IN,
  input  CLOCK,
  output [2:0] FUNCT3_OUT,
  output [6:0] FUNCT7_OUT
);

  Register #(.width(3)) register_1 (.D(FUNCT3_IN), .clk(CLOCK), .Q(FUNCT3_OUT));  // open: en, clr
  Register #(.width(7)) register_2 (.D(FUNCT7_IN), .clk(CLOCK), .Q(FUNCT7_OUT));  // open: en, clr
endmodule

module ID_EXC_PIPE_IMM_TO_B (
  input  [31:0] IMMEDIATE_IN,
  input  IMM_FLAG_IN,
  input  CLOCK,
  output [31:0] IMM_TO_B,
  output IMM_FLAG_OUT
);

  wire register_2_q;
  wire [31:0] register_1_q;

  Register #(.width(32)) register_1 (.D(IMMEDIATE_IN), .clk(CLOCK), .Q(register_1_q));  // open: en, clr
  Register #(.width(1)) register_2 (.D(IMM_FLAG_IN), .clk(CLOCK), .Q(register_2_q));  // open: en, clr
  Register #(.width(32)) register_3 (.D(register_1_q), .clk(CLOCK), .Q(IMM_TO_B));  // open: en, clr
  Register #(.width(1)) register_4 (.D(register_2_q), .clk(CLOCK), .Q(IMM_FLAG_OUT));  // open: en, clr
endmodule

module ID_REGFILE_PIPE_IMM_TO_DATA (
  input  [31:0] IMM_IN,
  input  FLAG_IN,
  input  CLOCK,
  output [31:0] IMM_TO_DATA,
  output FLAG_OUT
);

  wire [31:0] register_1_q, register_3_q, register_4_q;

  Register #(.width(32)) register_1 (.D(IMM_IN), .clk(CLOCK), .Q(register_1_q));  // open: en, clr
  Register #(.width(1)) register_2 (.D(FLAG_IN), .clk(CLOCK), .Q(FLAG_OUT));  // open: en, clr
  Register #(.width(32)) register_3 (.D(register_1_q), .Q(register_3_q));  // open: en, clk, clr
  Register #(.width(32)) register_4 (.D(register_3_q), .Q(register_4_q));  // open: en, clk, clr
  Register #(.width(32)) register_5 (.D(register_4_q), .Q(IMM_TO_DATA));  // open: en, clk, clr
endmodule

module ID_MEM_PIPE_IMM_TO_MemAddr (
  input  [31:0] IMM_IN,
  input  CLOCK,
  output [31:0] IMM_TO_MemAddr
);

  wire [31:0] register_1_q;

  Register #(.width(32)) register_1 (.D(IMM_IN), .clk(CLOCK), .Q(register_1_q));  // open: en, clr
  Register #(.width(32)) register_2 (.D(register_1_q), .clk(CLOCK), .Q(IMM_TO_MemAddr));  // open: en, clr
endmodule

module IMM_TO_PLUS_PC_AND_TO_DATA (
  input  [31:0] IMM_IN,
  input  FLAGE_IN,
  input  CLOCK,
  output [31:0] IMM_OUT,
  output FLAGE_OUT
);

  Register #(.width(32)) register_1 (.D(IMM_IN), .clk(CLOCK), .Q(IMM_OUT));  // open: en, clr
  Register #(.width(1)) register_2 (.D(FLAGE_IN), .clk(CLOCK), .Q(FLAGE_OUT));  // open: en, clr
endmodule

module REGFILE_EXC_PIPE (
  input  [31:0] OUT1_IN,
  input  [31:0] OUT2_IN,
  input  CLOCK,
  output [31:0] OUT1_OUT,
  output [31:0] OUT2_OUT
);

  Register #(.width(32)) register_1 (.D(OUT1_IN), .clk(CLOCK), .Q(OUT1_OUT));  // open: en, clr
  Register #(.width(32)) register_2 (.D(OUT2_IN), .clk(CLOCK), .Q(OUT2_OUT));  // open: en, clr
endmodule

module A_TO_MemAddr (
  input  [31:0] A_IN,
  input  CLOCK,
  output [31:0] A_OUT
);

  Register #(.trigger("falling"), .width(32)) register_1 (.D(A_IN), .clk(CLOCK), .Q(A_OUT));  // open: en, clr
endmodule

module B_TO_StoreValue (
  input  [31:0] B_IN,
  input  CLOCK,
  output [31:0] B_OUT
);

  Register #(.trigger("falling"), .width(32)) register_1 (.D(B_IN), .clk(CLOCK), .Q(B_OUT));  // open: en, clr
endmodule

module IMM_JALR_PIPE (
  input  [31:0] IMM_IN,
  input  JALR_FLAG_IN,
  input  CLOCK,
  output [31:0] IMM_OUT,
  output JALR_FLAG_OUT
);

  wire register_2_q;
  wire [31:0] register_1_q;

  Register #(.width(32)) register_1 (.D(IMM_IN), .clk(CLOCK), .Q(register_1_q));  // open: en, clr
  Register #(.width(1)) register_2 (.D(JALR_FLAG_IN), .clk(CLOCK), .Q(register_2_q));  // open: en, clr
  Register #(.width(32)) register_3 (.D(register_1_q), .clk(CLOCK), .Q(IMM_OUT));  // open: en, clr
  Register #(.width(1)) register_4 (.D(register_2_q), .clk(CLOCK), .Q(JALR_FLAG_OUT));  // open: en, clr
endmodule

module FUNCT3_TO_MemWidth (
  input  [2:0] FUNCT3_IN,
  input  CLOCK,
  output [2:0] FUNCT3_OUT
);

  Register #(.trigger("falling"), .width(3)) register_1 (.D(FUNCT3_IN), .clk(CLOCK), .Q(FUNCT3_OUT));  // open: en, clr
endmodule

module Relative_Jump_flags_PIPE (
  input  RelativeJumpFlag_IN,
  input  CLOCK,
  output RelativeJumpFlag_OUT
);

  Register #(.trigger("falling"), .width(1)) register_1 (
    .D(RelativeJumpFlag_IN), .clk(CLOCK), .Q(RelativeJumpFlag_OUT));  // open: en, clr
endmodule

module JALR_Result (
  input  [31:0] SUM_IN,
  input  JALR_FLAG_IN,
  input  CLOCK,
  output [31:0] SUM_OUT,
  output JALR_FLAG_OUT
);

  Register #(.trigger("falling"), .width(32)) register_1 (.D(SUM_IN), .clk(CLOCK), .Q(SUM_OUT));  // open: en, clr
  Register #(.trigger("falling"), .width(1)) register_2 (
    .D(JALR_FLAG_IN), .clk(CLOCK), .Q(JALR_FLAG_OUT));  // open: en, clr
endmodule

module Write_back_Data (
  input  Write_Flag_IN,
  input  [31:0] Data_IN,
  input  CLOCK,
  output Write_Flag_OUT,
  output [31:0] Data_OUT
);

  wire register_1_q, register_3_q;
  wire [31:0] register_2_q;

  Register #(.trigger("falling"), .width(1)) register_1 (
    .D(Write_Flag_IN), .clk(CLOCK), .Q(register_1_q));  // open: en, clr
  Register #(.trigger("falling"), .width(32)) register_2 (.D(Data_IN), .clk(CLOCK), .Q(register_2_q));  // open: en, clr
  Register #(.trigger("falling"), .width(1)) register_3 (
    .D(register_1_q), .clk(CLOCK), .Q(register_3_q));  // open: en, clr
  Register #(.trigger("falling"), .width(32)) register_4 (
    .D(register_2_q), .clk(CLOCK), .Q(Data_OUT));  // open: en, clr
  Register #(.trigger("falling"), .width(1)) register_5 (
    .D(register_3_q), .clk(CLOCK), .Q(Write_Flag_OUT));  // open: en, clr
endmodule

module Write_back_PC (
  input  signal_IN,
  input  CLOCK,
  output signal_OUT
);

  wire register_1_q, register_2_q;

  Register #(.trigger("falling"), .width(1)) register_1 (
    .D(signal_IN), .clk(CLOCK), .Q(register_1_q));  // open: en, clr
  Register #(.trigger("falling"), .width(1)) register_2 (
    .D(register_1_q), .clk(CLOCK), .Q(register_2_q));  // open: en, clr
  Register #(.trigger("falling"), .width(1)) register_3 (
    .D(register_2_q), .clk(CLOCK), .Q(signal_OUT));  // open: en, clr
endmodule

module Load_flag_PIPE (
  input  Load_flag_IN,
  input  CLOCK,
  output Load_data,
  output Load_Mem
);

  wire register_1_q;

  Register #(.trigger("falling"), .width(1)) register_1 (
    .D(Load_flag_IN), .clk(CLOCK), .Q(register_1_q));  // open: en, clr
  Register #(.trigger("falling"), .width(1)) register_2 (.D(register_1_q), .clk(CLOCK), .Q(Load_Mem));  // open: en, clr
  Register #(.trigger("falling"), .width(1)) register_3 (.D(Load_Mem), .clk(CLOCK), .Q(Load_data));  // open: en, clr
endmodule

module RD_PIPE (
  input  [4:0] RD_IN,
  input  f_IMM_Input,
  input  f_IMM_plus_PC_Input,
  input  f_store_PC_Input,
  input  f_ALU_data_Input,
  input  f_Load_Input,
  input  f_IMM_Output,
  input  f_IMM_plus_PC_Output,
  input  f_store_PC_Output,
  input  f_ALU_data_Output,
  input  f_Load_Output,
  input  CLOCK,
  output [4:0] RD_OUT,
  output write
);

  wire [2:0] controlled_buffer_1_out, controlled_buffer_6_out;
  wire [4:0] demultiplexer_1_out0, demultiplexer_1_out1, demultiplexer_1_out2, demultiplexer_1_out3,
       demultiplexer_1_out4, register_1_q, register_2_q, register_3_q, register_4_q, register_5_q,
       register_6_q, register_7_q, register_8_q, register_9_q, register_10_q;

  or or_1 (write, f_IMM_Output, f_IMM_plus_PC_Output, f_store_PC_Output, f_ALU_data_Output, f_Load_Output);
  assign controlled_buffer_1_out = f_IMM_Input ? 3'b000 : 3'bz;  // Controlled_Buffer controlled_buffer_1
  assign controlled_buffer_1_out = f_IMM_plus_PC_Input ? 3'b001 : 3'bz;  // Controlled_Buffer controlled_buffer_2
  assign controlled_buffer_1_out = f_store_PC_Input ? 3'b010 : 3'bz;  // Controlled_Buffer controlled_buffer_3
  assign controlled_buffer_1_out = f_ALU_data_Input ? 3'b011 : 3'bz;  // Controlled_Buffer controlled_buffer_4
  assign controlled_buffer_1_out = f_Load_Input ? 3'b100 : 3'bz;  // Controlled_Buffer controlled_buffer_5
  assign controlled_buffer_6_out = f_IMM_Output ? 3'b000 : 3'bz;  // Controlled_Buffer controlled_buffer_6
  assign controlled_buffer_6_out = f_IMM_plus_PC_Output ? 3'b001 : 3'bz;  // Controlled_Buffer controlled_buffer_7
  assign controlled_buffer_6_out = f_store_PC_Output ? 3'b010 : 3'bz;  // Controlled_Buffer controlled_buffer_8
  assign controlled_buffer_6_out = f_ALU_data_Output ? 3'b011 : 3'bz;  // Controlled_Buffer controlled_buffer_9
  assign controlled_buffer_6_out = f_Load_Output ? 3'b100 : 3'bz;  // Controlled_Buffer controlled_buffer_10
  Demultiplexer #(.select(3), .width(5)) demultiplexer_1 (
    .out0(demultiplexer_1_out0), .out1(demultiplexer_1_out1), .out2(demultiplexer_1_out2),
    .out3(demultiplexer_1_out3), .out4(demultiplexer_1_out4), .in(RD_IN), .sel(controlled_buffer_1_out));  // open: out5, out6, out7
  Register #(.width(5)) register_1 (.D(demultiplexer_1_out0), .clk(CLOCK), .Q(register_1_q));  // open: en, clr
  Register #(.width(5)) register_2 (.D(demultiplexer_1_out1), .clk(CLOCK), .Q(register_2_q));  // open: en, clr
  Register #(.width(5)) register_3 (.D(demultiplexer_1_out2), .clk(CLOCK), .Q(register_3_q));  // open: en, clr
  Register #(.width(5)) register_4 (.D(demultiplexer_1_out3), .clk(CLOCK), .Q(register_4_q));  // open: en, clr
  Register #(.width(5)) register_5 (.D(demultiplexer_1_out4), .clk(CLOCK), .Q(register_5_q));  // open: en, clr
  Register #(.width(5)) register_6 (.D(register_4_q), .clk(CLOCK), .Q(register_6_q));  // open: en, clr
  Register #(.width(5)) register_7 (.D(register_5_q), .clk(CLOCK), .Q(register_7_q));  // open: en, clr
  Register #(.width(5)) register_8 (.D(register_6_q), .clk(CLOCK), .Q(register_8_q));  // open: en, clr
  Register #(.width(5)) register_9 (.D(register_7_q), .clk(CLOCK), .Q(register_9_q));  // open: en, clr
  Register #(.width(5)) register_10 (.D(register_9_q), .clk(CLOCK), .Q(register_10_q));  // open: en, clr
  Multiplexer #(.select(3), .width(5)) multiplexer_1 (
    .in0(register_1_q), .in1(register_2_q), .in2(register_3_q), .in3(register_8_q), .in4(register_10_q),
    .out(RD_OUT), .sel(controlled_buffer_6_out));  // open: in5, in6, in7
endmodule

module Immediate_PIPE (
  input  [31:0] Immediate_IN,
  input  F_IMM_TO_DATA_IN,
  input  F_IMM_TO_PULS_PC_IN,
  input  F_IMM_TO_ALU_IN,
  input  Clock,
  output [31:0] To_ALU,
  output [31:0] To_MemWidth,
  output [31:0] To_Write_Back,
  output F_IMM_TO_DATA_OUT,
  output F_IMM_TO_PULS_PC_OUT,
  output F_IMM_TO_ALU_OUT
);

  wire register_2_q, register_3_q, register_6_q, register_7_q;

  Register #(.trigger("falling"), .width(32)) register_1 (.D(Immediate_IN), .clk(Clock), .Q(To_ALU));  // open: en, clr
  Register #(.trigger("falling"), .width(1)) register_2 (
    .D(F_IMM_TO_DATA_IN), .clk(Clock), .Q(register_2_q));  // open: en, clr
  Register #(.trigger("falling"), .width(1)) register_3 (
    .D(F_IMM_TO_PULS_PC_IN), .clk(Clock), .Q(register_3_q));  // open: en, clr
  Register #(.trigger("falling"), .width(1)) register_4 (
    .D(F_IMM_TO_ALU_IN), .clk(Clock), .Q(F_IMM_TO_ALU_OUT));  // open: en, clr
  Register #(.trigger("falling"), .width(32)) register_5 (.D(To_ALU), .clk(Clock), .Q(To_MemWidth));  // open: en, clr
  Register #(.trigger("falling"), .width(1)) register_6 (
    .D(register_2_q), .clk(Clock), .Q(register_6_q));  // open: en, clr
  Register #(.trigger("falling"), .width(1)) register_7 (
    .D(register_3_q), .clk(Clock), .Q(register_7_q));  // open: en, clr
  Register #(.trigger("falling"), .width(32)) register_8 (
    .D(To_MemWidth), .clk(Clock), .Q(To_Write_Back));  // open: en, clr
  Register #(.trigger("falling"), .width(1)) register_9 (
    .D(register_6_q), .clk(Clock), .Q(F_IMM_TO_DATA_OUT));  // open: en, clr
  Register #(.trigger("falling"), .width(1)) register_10 (
    .D(register_7_q), .clk(Clock), .Q(F_IMM_TO_PULS_PC_OUT));  // open: en, clr
endmodule

module ID_Write_Back (
  input  [4:0] RD_IN,
  input  Write_IN,
  input  Clock,
  output [4:0] RD_OUT,
  output Write_OUT
);

  wire register_2_q, register_4_q;
  wire [4:0] register_1_q, register_3_q;

  Register #(.trigger("falling"), .width(5)) register_1 (.D(RD_IN), .clk(Clock), .Q(register_1_q));  // open: en, clr
  Register #(.trigger("falling"), .width(1)) register_2 (.D(Write_IN), .clk(Clock), .Q(register_2_q));  // open: en, clr
  Register #(.trigger("falling"), .width(5)) register_3 (
    .D(register_1_q), .clk(Clock), .Q(register_3_q));  // open: en, clr
  Register #(.trigger("falling"), .width(1)) register_4 (
    .D(register_2_q), .clk(Clock), .Q(register_4_q));  // open: en, clr
  Register #(.trigger("falling"), .width(5)) register_5 (.D(register_3_q), .clk(Clock), .Q(RD_OUT));  // open: en, clr
  Register #(.trigger("falling"), .width(1)) register_6 (
    .D(register_4_q), .clk(Clock), .Q(Write_OUT));  // open: en, clr
endmodule

module ID_EXC (
  input  [2:0] FUNCT3_IN,
  input  [6:0] FUNCT7_IN,
  input  [31:0] OUT1_IN,
  input  [31:0] OUT2_IN,
  input  CLOCK,
  output [2:0] FUNCT3_OUT,
  output [6:0] FUNCT7_OUT,
  output [31:0] OUT1_OUT,
  output [31:0] OUT2_OUT
);

  Register #(.trigger("falling"), .width(3)) register_1 (.D(FUNCT3_IN), .clk(CLOCK), .Q(FUNCT3_OUT));  // open: en, clr
  Register #(.trigger("falling"), .width(7)) register_2 (.D(FUNCT7_IN), .clk(CLOCK), .Q(FUNCT7_OUT));  // open: en, clr
  Register #(.trigger("falling"), .width(32)) register_3 (.D(OUT1_IN), .clk(CLOCK), .Q(OUT1_OUT));  // open: en, clr
  Register #(.trigger("falling"), .width(32)) register_4 (.D(OUT2_IN), .clk(CLOCK), .Q(OUT2_OUT));  // open: en, clr
endmodule

module Store_pc (
  input  [31:0] pc_in,
  input  Clock,
  output [31:0] pc_out
);

  wire [31:0] register_1_q, register_2_q;

  Register #(.trigger("falling"), .width(32)) register_1 (.D(pc_in), .clk(Clock), .Q(register_1_q));  // open: en, clr
  Register #(.trigger("falling"), .width(32)) register_2 (
    .D(register_1_q), .clk(Clock), .Q(register_2_q));  // open: en, clr
  Register #(.trigger("falling"), .width(32)) register_3 (.D(register_2_q), .clk(Clock), .Q(pc_out));  // open: en, clr
endmodule

module Signals_off_NoOperation (
  input  S1,
  input  S2,
  input  S3,
  input  S4,
  input  S5,
  input  S6,
  input  S7,
  input  S8,
  input  S9,
  input  S10,
  input  S_OFF,
  output S1_OUT,
  output S2_OUT,
  output S3_OUT,
  output S4_OUT,
  output S5_OUT,
  output S6_OUT,
  output S7_OUT,
  output S8_OUT,
  output S9_OUT,
  output S10_OUT
);

  wire not_1_out;

  not not_1 (not_1_out, S_OFF);
  and and_1 (S1_OUT, S1, not_1_out);
  and and_2 (S2_OUT, S2, not_1_out);
  and and_3 (S3_OUT, S3, not_1_out);
  and and_4 (S4_OUT, S4, not_1_out);
  and and_5 (S5_OUT, S5, not_1_out);
  and and_6 (S6_OUT, S6, not_1_out);
  and and_7 (S7_OUT, S7, not_1_out);
  and and_8 (S8_OUT, S8, not_1_out);
  and and_9 (S9_OUT, S9, not_1_out);
  and and_10 (S10_OUT, S10, not_1_out);
endmodule

module ID_EXC1 (
  input  [4:0] RS1_IN,
  input  [4:0] RS2_IN,
  input  [2:0] FUNCT3_IN,
  input  [6:0] FUNCT7_IN,
  input  [31:0] OUT1_IN,
  input  [31:0] OUT2_IN,
  input  CLOCK,
  output [4:0] RS1_OUT,
  output [4:0] RS2_OUT,
  output [2:0] FUNCT3_OUT,
  output [6:0] FUNCT7_OUT,
  output [31:0] OUT1_OUT,
  output [31:0] OUT2_OUT
);

  Register #(.trigger("falling"), .width(5)) register_1 (.D(RS1_IN), .clk(CLOCK), .Q(RS1_OUT));  // open: en, clr
  Register #(.trigger("falling"), .width(5)) register_2 (.D(RS2_IN), .clk(CLOCK), .Q(RS2_OUT));  // open: en, clr
  Register #(.trigger("falling"), .width(3)) register_3 (.D(FUNCT3_IN), .clk(CLOCK), .Q(FUNCT3_OUT));  // open: en, clr
  Register #(.trigger("falling"), .width(7)) register_4 (.D(FUNCT7_IN), .clk(CLOCK), .Q(FUNCT7_OUT));  // open: en, clr
  Register #(.trigger("falling"), .width(32)) register_5 (.D(OUT1_IN), .clk(CLOCK), .Q(OUT1_OUT));  // open: en, clr
  Register #(.trigger("falling"), .width(32)) register_6 (.D(OUT2_IN), .clk(CLOCK), .Q(OUT2_OUT));  // open: en, clr
endmodule

module EXMEM_Forward_Pipe (
  input  [31:0] ALUResult_IN,
  input  [4:0] RD_IN,
  input  Write_IN,
  input  Clock,
  output [31:0] ALUResult_OUT,
  output [4:0] RD_OUT,
  output Write_OUT
);

  wire register_3_q;
  wire [4:0] register_2_q;

  Register #(.trigger("falling"), .width(32)) register_1 (
    .D(ALUResult_IN), .clk(Clock), .Q(ALUResult_OUT));  // open: en, clr
  Register #(.trigger("falling"), .width(5)) register_2 (.D(RD_IN), .clk(Clock), .Q(register_2_q));  // open: en, clr
  Register #(.trigger("falling"), .width(1)) register_3 (.D(Write_IN), .clk(Clock), .Q(register_3_q));  // open: en, clr
  Register #(.trigger("falling"), .width(5)) register_4 (.D(register_2_q), .clk(Clock), .Q(RD_OUT));  // open: en, clr
  Register #(.trigger("falling"), .width(1)) register_5 (
    .D(register_3_q), .clk(Clock), .Q(Write_OUT));  // open: en, clr
endmodule

module Forwarding_Unit (
  input  [4:0] RS1,
  input  [4:0] EXMEM_RD,
  input  EXMEM_Write,
  input  [4:0] MEMWB_RD,
  input  MEMWB_Write,
  input  [4:0] RS2,
  output ForwardA_EXMEM,
  output ForwardA_MEMWB,
  output ForwardB_EXMEM,
  output ForwardB_MEMWB
);

  wire and_3_out, and_4_out, comparator_1_eq, comparator_2_eq, comparator_3_eq, comparator_4_eq,
       EXMEM_nonzero_out, MEMWB_nonzero_out, not_1_out, not_2_out;

  Comparator #(.mode("unsigned"), .width(5)) comparator_1 (
    .a(RS1), .b(EXMEM_RD), .eq(comparator_1_eq));  // open: gt, lt
  or EXMEM_nonzero (EXMEM_nonzero_out, EXMEM_RD[0], EXMEM_RD[1], EXMEM_RD[2], EXMEM_RD[3], EXMEM_RD[4]);
  or MEMWB_nonzero (MEMWB_nonzero_out, MEMWB_RD[0], MEMWB_RD[1], MEMWB_RD[2], MEMWB_RD[3], MEMWB_RD[4]);
  Comparator #(.mode("unsigned"), .width(5)) comparator_2 (
    .a(EXMEM_RD), .b(RS2), .eq(comparator_2_eq));  // open: gt, lt
  Comparator #(.mode("unsigned"), .width(5)) comparator_3 (
    .a(RS1), .b(MEMWB_RD), .eq(comparator_3_eq));  // open: gt, lt
  Comparator #(.mode("unsigned"), .width(5)) comparator_4 (
    .a(MEMWB_RD), .b(RS2), .eq(comparator_4_eq));  // open: gt, lt
  and and_1 (ForwardA_EXMEM, comparator_1_eq, EXMEM_nonzero_out, EXMEM_Write);
  not not_1 (not_1_out, ForwardA_EXMEM);
  and and_2 (ForwardB_EXMEM, comparator_2_eq, EXMEM_nonzero_out, EXMEM_Write);
  not not_2 (not_2_out, ForwardB_EXMEM);
  and and_3 (and_3_out, comparator_3_eq, MEMWB_nonzero_out, MEMWB_Write);
  and and_4 (and_4_out, comparator_4_eq, MEMWB_nonzero_out, MEMWB_Write);
  and and_5 (ForwardA_MEMWB, not_1_out, and_3_out);
  and and_6 (ForwardB_MEMWB, not_2_out, and_4_out);
endmodule

module Thumb_Decompresser (
  input  [15:0] Instruction_IN,
  output [31:0] Instruction_OUT
);

  wire and_1_out, comparator_1_eq, comparator_2_eq, comparator_3_eq, not_1_out, or_1_out;
  wire [31:0] alu_imm_1_instruction_out, alu_reg_1_intruction_out, branch_control_1_instruction_out,
       jal_1_instruction_out, load_1_instruction_out, lui_1_instruction_out, multiplexer_1_out,
       multiply_1_instruction_out, store_1_instruction_out, thumb_toggle_1_out_1;

  Comparator #(.mode("unsigned"), .width(3)) comparator_1 (
    .a(Instruction_IN[2:0]), .b(3'b110), .eq(comparator_1_eq));  // open: gt, lt
  Comparator #(.mode("unsigned"), .width(3)) comparator_2 (
    .a(Instruction_IN[10:8]), .b(3'b010), .eq(comparator_2_eq));  // open: gt, lt
  Comparator #(.mode("unsigned"), .width(3)) comparator_3 (
    .a(Instruction_IN[10:8]), .b(3'b011), .eq(comparator_3_eq));  // open: gt, lt
  or or_1 (or_1_out, comparator_2_eq, comparator_3_eq);
  and and_1 (and_1_out, comparator_1_eq, or_1_out);
  Load load_1 (
    .rd(Instruction_IN[7:3]), .funct3(Instruction_IN[10:8]), .rs1(Instruction_IN[15:11]),
    .instruction_OUT(load_1_instruction_out));
  ALU_Imm alu_imm_1 (
    .rd(Instruction_IN[7:3]), .funct3(Instruction_IN[10:8]), .rs1(Instruction_IN[7:3]),
    .imm(Instruction_IN[15:11]), .instruction_OUT(alu_imm_1_instruction_out));
  Store store_1 (
    .funct3(Instruction_IN[10:8]), .rs1(Instruction_IN[7:3]), .rs2(Instruction_IN[15:11]),
    .instruction_OUT(store_1_instruction_out));
  ALU_Reg alu_reg_1 (
    .rd(Instruction_IN[7:3]), .funct3(Instruction_IN[10:8]), .rs1(Instruction_IN[7:3]),
    .rs2(Instruction_IN[15:11]), .intruction_OUT(alu_reg_1_intruction_out));
  JAL jal_1 (
    .rd(Instruction_IN[7:3]), .eight_ten(Instruction_IN[10:8]), .eleven_fifteen(Instruction_IN[15:11]),
    .instruction_OUT(jal_1_instruction_out));
  LUI lui_1 (
    .rd(Instruction_IN[7:3]), .eight_ten(Instruction_IN[10:8]), .eleven_fifteen(Instruction_IN[15:11]),
    .instruction_OUT(lui_1_instruction_out));
  Branch_Control branch_control_1 (
    .rs1(Instruction_IN[15:11]), .funct3(Instruction_IN[10:8]), .imm(Instruction_IN[7:3]),
    .instruction_OUT(branch_control_1_instruction_out));
  Multiply multiply_1 (
    .rd(Instruction_IN[7:3]), .funct3(Instruction_IN[10:8]), .rs1(Instruction_IN[7:3]),
    .rs2(Instruction_IN[15:11]), .instruction_OUT(multiply_1_instruction_out));
  Multiplexer #(.select(3), .width(32)) multiplexer_1 (
    .in0(load_1_instruction_out), .in1(alu_imm_1_instruction_out), .in2(store_1_instruction_out),
    .in3(alu_reg_1_intruction_out), .in4(jal_1_instruction_out), .in5(lui_1_instruction_out),
    .in6(branch_control_1_instruction_out), .in7(multiply_1_instruction_out), .out(multiplexer_1_out),
    .sel(Instruction_IN[2:0]));
  Thumb_Toggle thumb_toggle_1 (.out_1(thumb_toggle_1_out_1));
  not not_1 (not_1_out, and_1_out);
  Multiplexer #(.width(32)) multiplexer_2 (
    .in0(thumb_toggle_1_out_1), .in1(multiplexer_1_out), .out(Instruction_OUT), .sel(not_1_out));
endmodule

module Load (
  input  [4:0] rd,
  input  [2:0] funct3,
  input  [4:0] rs1,
  output [31:0] instruction_OUT
);


  assign instruction_OUT = {{12{1'b0}}, rs1, funct3, rd, 7'b0000011};
endmodule

module ALU_Imm (
  input  [4:0] rd,
  input  [2:0] funct3,
  input  [4:0] rs1,
  input  [4:0] imm,
  output [31:0] instruction_OUT
);

  wire comparator_1_eq, comparator_2_eq, or_1_out;
  wire [11:0] decodeimm_1_decode;

  Comparator #(.mode("unsigned"), .width(3)) comparator_1 (
    .a(funct3), .b(3'b001), .eq(comparator_1_eq));  // open: gt, lt
  Comparator #(.mode("unsigned"), .width(3)) comparator_2 (
    .a(funct3), .b(3'b101), .eq(comparator_2_eq));  // open: gt, lt
  DecodeImm decodeimm_1 (.imm(imm), .Decode(decodeimm_1_decode));
  or or_1 (or_1_out, comparator_1_eq, comparator_2_eq);
  Multiplexer #(.width(12)) multiplexer_1 (
    .in0(decodeimm_1_decode), .in1({{7{1'b0}}, imm}), .out(instruction_OUT[31:20]), .sel(or_1_out));

  assign instruction_OUT[19:0] = {rs1, funct3, rd, 7'b0010011};
endmodule

module Store (
  input  [2:0] funct3,
  input  [4:0] rs1,
  input  [4:0] rs2,
  output [31:0] instruction_OUT
);


  assign instruction_OUT = {{7{1'b0}}, rs2, rs1, funct3, 12'h23};
endmodule

module ALU_Reg (
  input  [4:0] rd,
  input  [2:0] funct3,
  input  [4:0] rs1,
  input  [4:0] rs2,
  output [31:0] intruction_OUT
);


  assign intruction_OUT = {{7{1'b0}}, rs2, rs1, funct3, rd, 7'b0110011};
endmodule

module JAL (
  input  [4:0] rd,
  input  [2:0] eight_ten,
  input  [4:0] eleven_fifteen,
  output [31:0] instruction_OUT
);


  assign instruction_OUT = {3'b000, eleven_fifteen, eight_ten, {9{1'b0}}, rd, 7'b1101111};
endmodule

module LUI (
  input  [4:0] rd,
  input  [2:0] eight_ten,
  input  [4:0] eleven_fifteen,
  output [31:0] instruction_OUT
);


  assign instruction_OUT = {{12{1'b0}}, eleven_fifteen, eight_ten, rd, 7'b0110111};
endmodule

module Branch_Control (
  input  [4:0] rs1,
  input  [2:0] funct3,
  input  [4:0] imm,
  output [31:0] instruction_OUT
);

  wire comparator_1_eq, comparator_2_eq, or_1_out;

  Comparator #(.mode("unsigned"), .width(3)) comparator_1 (
    .a(funct3), .b(3'b010), .eq(comparator_1_eq));  // open: gt, lt
  Comparator #(.mode("unsigned"), .width(3)) comparator_2 (
    .a(funct3), .b(3'b011), .eq(comparator_2_eq));  // open: gt, lt
  or or_1 (or_1_out, comparator_1_eq, comparator_2_eq);
  Multiplexer #(.width(7)) multiplexer_1 (
    .in0(7'b1100011), .in1({7{1'b1}}), .out(instruction_OUT[6:0]), .sel(or_1_out));
  DecodeImm decodeimm_1 (
    .imm(rs1),
    .Decode({instruction_OUT[31], instruction_OUT[7], instruction_OUT[30:25], instruction_OUT[11:8]}));

  assign instruction_OUT[24:12] = {{5{1'b0}}, imm, funct3};
endmodule

module Multiply (
  input  [4:0] rd,
  input  [2:0] funct3,
  input  [4:0] rs1,
  input  [4:0] rs2,
  output [31:0] instruction_OUT
);


  assign instruction_OUT = {7'b0000001, rs2, rs1, funct3, rd, 7'b0110011};
endmodule

module Thumb_Toggle (
  output [31:0] out_1
);


  assign out_1 = 32'h7f;
endmodule

module DecodeImm (
  input  [4:0] imm,
  output [11:0] Decode
);


  assign Decode = {4'b0000, imm, 3'b000};
endmodule

module Instructions_32Bits (
  input  [15:0] LowerHalf,
  input  [15:0] UpperHalf,
  output [31:0] Instructions_OUT
);


  assign Instructions_OUT = {UpperHalf, LowerHalf};
endmodule
